// Logisim project Simulacion.circ as structural Verilog: 3 circuits, main circuit Nex state
module Nex_state (
  input  S0,
  input  S1,
  input  Ta,
  input  Tb,
  input  E,
  input  Pav,
  input  Pb,
  input  nS0,
  input  nS1,
  output S0_prime,
  output S1_prime
);

  wire and_1_out, and_2_out, and_3_out, and_4_out, and_5_out, and_6_out, and_7_out, and_8_out, and_9_out,
       not_1_out, not_2_out, not_3_out, or_2_out, or_3_out;

  not not_1 (not_1_out, Ta);
  not not_2 (not_2_out, Tb);
  not not_3 (not_3_out, E);
  and and_1 (and_1_out, S1, nS0);
  and and_2 (and_2_out, and_1_out, not_3_out);
  and and_3 (and_3_out, and_2_out, not_2_out);
  and and_4 (and_4_out, Pav, and_5_out);
  and and_5 (and_5_out, nS0, nS1);
  and and_6 (and_6_out, nS1, S0);
  and and_7 (and_7_out, and_6_out, not_3_out);
  and and_8 (and_8_out, Pb, and_2_out);
  and and_9 (and_9_out, and_5_out, not_1_out);
  or or_1 (S1_prime, and_2_out, and_7_out);
  or or_2 (or_2_out, and_3_out, and_8_out);
  or or_3 (or_3_out, and_4_out, and_9_out);
  or or_4 (S0_prime, or_2_out, or_3_out);
endmodule

module Output_State (
  input  S1,
  input  S0,
  output LA_Rojo,
  output LA_Amarilo,
  output LA_Verde,
  output LB_Rojo,
  output LB_Amarillo,
  output LB_Verde,
  output Peaton_Av_Rojo,
  output Peaton_Av_Verde,
  output Peaton_B_Rojo,
  output Peaton_B_Verde
);

  wire not_2_out;

  not not_1 (LB_Rojo, S1);
  not not_2 (not_2_out, S0);
  and and_1 (LA_Amarilo, LB_Rojo, S0);
  and and_2 (LA_Verde, LB_Rojo, not_2_out);
  and and_3 (LB_Amarillo, S1, S0);
  and and_4 (LB_Verde, S1, not_2_out);
  or or_1 (Peaton_Av_Rojo, LB_Rojo, S0);
  or or_2 (Peaton_B_Rojo, S0, S1);

  assign LA_Rojo = S1;
  assign Peaton_Av_Verde = LB_Verde;
  assign Peaton_B_Verde = LA_Verde;
endmodule

module completed (
);

  wire clock_1_out, d_ff_1_q, d_ff_1_qn, d_ff_2_q, d_ff_2_qn, nex_state_1_s0_prime, nex_state_1_s1_prime,
       output_state_1_la_amarilo, output_state_1_la_rojo, output_state_1_la_verde,
       output_state_1_lb_amarillo, output_state_1_lb_rojo, output_state_1_lb_verde,
       output_state_1_peaton_av_rojo, output_state_1_peaton_av_verde, output_state_1_peaton_b_rojo,
       output_state_1_peaton_b_verde;

  Nex_state nex_state_1 (
    .S1(d_ff_2_q), .nS0(d_ff_1_qn), .Tb(1'b0), .E(1'b0), .nS1(d_ff_2_qn), .Pav(1'b0), .Pb(1'b0), .Ta(1'b1),
    .S0(d_ff_1_q), .S0_prime(nex_state_1_s0_prime), .S1_prime(nex_state_1_s1_prime));
  Clock clock_1 (.out(clock_1_out));
  D_Flip_Flop d_ff_1 (
    .clk(clock_1_out), .D(nex_state_1_s0_prime), .Q(d_ff_1_q), .Qn(d_ff_1_qn));  // open: preset, en, reset
  D_Flip_Flop d_ff_2 (
    .clk(clock_1_out), .D(nex_state_1_s1_prime), .Q(d_ff_2_q), .Qn(d_ff_2_qn));  // open: preset, en, reset
  Output_State output_state_1 (
    .S1(d_ff_2_q), .S0(d_ff_1_q), .LA_Rojo(output_state_1_la_rojo), .LA_Amarilo(output_state_1_la_amarilo),
    .LA_Verde(output_state_1_la_verde), .LB_Rojo(output_state_1_lb_rojo),
    .LB_Amarillo(output_state_1_lb_amarillo), .LB_Verde(output_state_1_lb_verde),
    .Peaton_Av_Rojo(output_state_1_peaton_av_rojo), .Peaton_Av_Verde(output_state_1_peaton_av_verde),
    .Peaton_B_Rojo(output_state_1_peaton_b_rojo), .Peaton_B_Verde(output_state_1_peaton_b_verde));
  LED led_1 (.in(output_state_1_la_rojo));
  LED led_2 (.in(output_state_1_la_amarilo));
  LED led_3 (.in(output_state_1_la_verde));
  LED led_4 (.in(output_state_1_peaton_av_rojo));
  LED led_5 (.in(output_state_1_peaton_av_verde));
  LED led_6 (.in(output_state_1_peaton_b_rojo));
  LED led_7 (.in(output_state_1_lb_rojo));
  LED led_8 (.in(output_state_1_peaton_b_verde));
  LED led_9 (.in(output_state_1_lb_amarillo));
  LED led_10 (.in(output_state_1_lb_verde));

  // Notes on the sheet:
  //   Semaforo Av
  //   Peaton AV
  //   Semaforo Blv
  //   Peaton Blv
endmodule
